// Digital circuit state.dig as structural Verilog
module state (
  input  [15:0] Lookup,
  input  from_q,
  input  Activating,
  output out_4,
  output _1,
  output _0,
  output _1_2,
  output _0_2,
  output H,
  output H1,
  output H0,
  output out_12,
  output _0_3,
  output _1_3,
  output _00,
  output _01,
  output _10,
  output _11,
  output out_19,
  output SHL,
  output SHR
);

  wire Active_value, Am_q_value, and_2_out, not_1_out, not_2_out, or_1_out;
  wire [15:0] and_1_out;

  not not_1 (not_1_out, Activating);
  flipflop Am_q (.Data(from_q), .Write(not_1_out), .Value(Am_q_value));
  flipflop Active (.Data(Am_q_value), .Write(Activating), .Value(Active_value));
  assign and_1_out = 16'h1 & Lookup;  // And and_1, 16 bits wide
  and and_2 (and_2_out, Active_value, ~Activating);  // And
  OR or_1 (.In(and_1_out), .Out(or_1_out));
  CONTROL #(.generic("bitWidth := 1;")) control_1 (.Control(and_2_out), .In(or_1_out), .Out(SHL));
  CONTROL #(.generic("bitWidth := 1;")) control_2 (.Control(and_2_out), .In(not_2_out), .Out(SHR));
  not not_2 (not_2_out, or_1_out);
  CONTROL #(.generic("bitWidth := 16;")) control_3 (
    .Control(and_2_out), .In(Lookup),
    .Out({out_4, _1, _0, out_19, _00, _01, _10, _11, out_12, _0_3, _1_3, _1_2, _0_2, H, H1, H0}));

  // Notes on the sheet:
  //   Lookup: 16 bits, each corresponding to one tape symbol
  //   from_q: 1 if the current q is indicating that this is q'
  //   Activating: 1 when activated should be updated
  //   Phase 1: not Activating
  //   Send out all info
  //   Update Am q'
  //   Phase 2: Activating
  //   Stop writing to Am q'
  //   Stop sending any info
  //   Update Active
endmodule

/* Code that sets the parameters or builds the circuit:
shift := 0x3000;
*/
