// Digital circuit tape.dig as structural Verilog
module tape (
);

  wire tapeseg_1_lout, tapeseg_2_lout, tapeseg_2_rout, tapeseg_3_rout, undriven, undriven_3, undriven_4;
  wire [3:0] tapeseg_1_value, undriven_2;

  tapeseg tapeseg_1 (
    .Write(undriven), .Value(tapeseg_1_value), .SHR(undriven_4), .SHL(undriven_3), .Data(undriven_2),
    .Lout(tapeseg_1_lout), .Rin(tapeseg_2_rout));  // open: Lin, Rout
  tapeseg tapeseg_2 (
    .Write(undriven), .Value(tapeseg_1_value), .SHR(undriven_4), .SHL(undriven_3), .Data(undriven_2),
    .Lin(tapeseg_1_lout), .Rout(tapeseg_2_rout), .Lout(tapeseg_2_lout), .Rin(tapeseg_3_rout));
  tapeseg tapeseg_3 (
    .Write(undriven), .Value(tapeseg_1_value), .SHR(undriven_4), .SHL(undriven_3), .Data(undriven_2),
    .Lin(tapeseg_2_lout), .Rout(tapeseg_3_rout));  // open: Lout, Rin
endmodule
