// Digital circuit tapecell.dig as structural Verilog
module tapecell (
  input  [3:0] Data,
  input  Write,
  output [3:0] Value
);

  flipflop flipflop_1 (.Data(Data[0]), .Write(Write), .Value(Value[0]));
  flipflop flipflop_2 (.Data(Data[1]), .Write(Write), .Value(Value[1]));
  flipflop flipflop_3 (.Data(Data[2]), .Write(Write), .Value(Value[2]));
  flipflop flipflop_4 (.Data(Data[3]), .Write(Write), .Value(Value[3]));
endmodule
