// Digital circuit testing.dig as structural Verilog
module testing (
  input  clk
);

  wire g0, not_1_out, or_1_out, or_2_out, t, t3, undriven, undriven_2, undriven_3, undriven_4, undriven_5,
       undriven_6;
  wire [15:0] driverinvsel_1_out, driverinvsel_2_out, driverinvsel_3_out;

  or or_1 (or_1_out, clk, or_1_out);
  not not_1 (not_1_out, or_1_out);
  assign driverinvsel_1_out = ~clk ? 16'h2000 : 16'bz;  // DriverInvSel driverinvsel_1
  assign driverinvsel_2_out = ~clk ? 16'h400 : 16'bz;  // DriverInvSel driverinvsel_2
  assign driverinvsel_3_out = ~clk ? 16'h10 : 16'bz;  // DriverInvSel driverinvsel_3
  or or_2 (or_2_out, t, not_1_out);
  // state #(.generic("shift := 0x3000;")) testing: pin names not known; wires that end beside it: or_2_out, clk, driverinvsel_1_out, g0
  // state #(.generic("shift := 0x3000;")) testing2: pin names not known; wires that end beside it: g0, clk, driverinvsel_2_out, t3
  // state #(.generic("shift := 0x3000;")) testing3: pin names not known; wires that end beside it: t3, clk, driverinvsel_3_out, t
  LED led_1 (.in(undriven));
  LED led_2 (.in(undriven_2));
  LED led_3 (.in(undriven_3));
  LED led_4 (.in(undriven_4));
  LED led_5 (.in(undriven_5));
  LED led_6 (.in(undriven_6));

  // Other names for the same wires on the sheet: t2 = g0
endmodule
